# Fritzing sketch Porcoduino (saved by Fritzing 0.9.0b)
breadboards: 1

parts:
  Part1 = Arduino Uno (Rev3)
  IC1 = L293D [package=THT]
  L2 = Solenoid
  L1 = Solenoid
  VCC1 = 4 x AAA Battery Mount
  Part2 = Arduino Xbee Libellium Shield [part_number=Part1]

nets:
  N1: Part1.D8, IC1.In_2
  N2: Part1.D11_PWM/MOSI, IC1.Enable_2
  N3: Part1.D12/MISO, IC1.In_3
  N4: Part1.D13/SCK, IC1.In_4
  N5: Part1.GND, IC1.0V, VCC1.-
  N6: Part1.5V, IC1.+V
  N7: IC1.Enable_1, Part2.D3
  N8: IC1.In_1, Part2.D7
  N9: IC1.Out_1_(_Controlled_by_Enable_1_), L2.pin2
  N10: IC1.Out_2_(_Controlled_by_Enable_1_), L2.pin1
  N11: IC1.+Vmotor, VCC1.+
  N12: IC1.Out_3_(_Controlled_by_Enable_2_), L1.pin1
  N13: IC1.Out_4_(_Controlled_by_Enable_2_), L1.pin2
